// Logisim project badApple.circ as structural Verilog: 1 circuit, main circuit main
module main (
  input  Toggle
);

  wire clock_1_out, Reset_out;
  wire [11:0] counter_1_q;
  wire [63:0] rom_1_data;

  Button Reset (.out(Reset_out));
  Clock clock_1 (.out(clock_1_out));
  Counter #(.max('hfff), .width(12)) counter_1 (
    .clr(Reset_out), .up(Toggle), .count(Toggle), .clk(clock_1_out), .Q(counter_1_q));  // open: load, D, carry
  ROM #(.addrWidth(12), .dataWidth(64)) rom_1 (.addr(counter_1_q), .data(rom_1_data));
  DotMatrix #(.inputtype("row"), .matrixcols(8), .matrixrows(8)) dotmatrix_1 (
    .row0(rom_1_data[63:56]), .row1(rom_1_data[55:48]), .row2(rom_1_data[47:40]), .row3(rom_1_data[39:32]),
    .row4(rom_1_data[31:24]), .row5(rom_1_data[23:16]), .row6(rom_1_data[15:8]), .row7(rom_1_data[7:0]));

  // Notes on the sheet:
  //   contents of rom_1 (hex, n*v repeats v):
  //   14*0 40808080 e0e0e0e0e0c0c0c0 e0e0e0e0c0808080 c0c0c0c080808000 c1c1c1c181818000 838383c383830101
  //   8383838783830301 87c7878787030303 8787c78787870783 c7c7c7c7c7838383 c7c7c7c7c3c3c383
  //   c7e7e7e7c3c3c3c1 c3e7e7e7e3c3c3c1 e3e3e7e3e3e3c3c1 e3e3e7e3e3e3e1c1 e3e3f3f3e3e3e3e1
  //   e3e7f7e7e3e3e3c3 e7e7e7e7e3e3c3c3 e7e7e7e7e7c3c3c7 e7e7e7e7e7c7c7c7 e7e7e7e7c7c7c7c7
  //   c7e7efe7c7c7c7c7 efe7efefc7c7c7c7 e7e7efe7e7c7c7c7 e7e7e7e7e7e7c7e7 f7e7e7e7e7e3e3e3
  //   f7e7e7e7e7e3e3e3 f7e7f7e7e7e3e3e3 f7e7f7f7e7e3e3e3 ffe7f7f7e7e3e3e3 f7e7f7e7e7e3e3e3
  //   e7e7e7e7e7e7e7e7 ffe7e7e7e7e7c7e7 ffe7e7e7e7c7c7c7 efe7efe7e7c7c7c7 efe7efefe7c7c7c7
  //   ffe7efefe7c7c7c7 efe7efe7e7e7c7e7 e7e7e7e7e7e7e7e7 ffe7e7e7e7e7e3e7 ffe7e7e7e7e3e3e3
  //   e7e7e7e7e7c7c3c3 c7e7e7e7e7c7c7c3 c7c7c7e7c7c78787 8787cfcfcf8f8f07 8f8f8f8f8f8f8f0f
  //   9f8f8f8f9f8f8f83 ff9f8f8f9f9f8b87 ff9f8f8f9f9f8387 ffdf8f8f9fdb8387 ffcf8f8f9fdb8787
  //   ffcf8f8f9fdbc787 ffcfcf8f9fcbc787 ffcf8f8f9fcbc787 ffcf8f8f9fdbc787 ffcf8f8f9fdbc787
  //   ffcf8f8f9fdbc787 df8f8f8f9f93c787 df8f8f8f9f938787 df8f8f8f9f978787 df8f8f8f9f978787
  //   df8f8f8f97878787 9f8f8f8f97878787 6*9f8f8f8f87878787 df8f8f8f87878787 df8f8f8f87878787
  //   cf8f8f8f87878787 cf8f878f87878787 cf8f878f8f838787 cf8f878f8f938787 c78f878f8f8f8387
  //   c7c787878f8f8f89 c7c7c7878f8f9f9f ffc787878f8f9f1f ff8f8f8f8f8f3f3f ff3f1f1f1f1f3f3f
  //   7f3f3f3f3f3f3f3f ff7f7f7f7f1f0701 efef434303273f3f ffffffffffffffbf f7ffffffffffffff
  //   f7f7ffffffffffff ffe7e7ffffffffff ffffefe7efffffff ffffffefe7efffff ffffffffe7e7ffff
  //   ffffffffefe7efff ffffffffefe7efff ffffffffe7e7efff ffffffefe7efffff ffffffe7e7ffffff
  //   ffffe7e7efffffff ffffe7e7efffffff ffffe7e7efffffff ffffefc7e7ffffff ffffefc7c7ffffff
  //   ffffffcfc7efffff ffffffcfc7efffff ffffffcfc7efffff ffffffefc7efffff 1f7f67e7efffff
  //   4*f8f0d01818100000 fffefe3707020000 70fffffffe40000 101037fffff42 10303077fffffe3 7070f0f1fffffff
  //   7c3c3d7f7efcfeff f8f0e47cf0f0e0f8 f8f0e0e8f0e0c0d0 f8f0e0c8f0e0e080 f8f0e0c8d8f0e0e0
  //   fcf8f0f0d8f0f0e0 f8f8f0f0f8f0e0e0 f8f8f0f0f0f0e0e0 ecf8f8f0f0f0e0e0 ec7cfcf0f0f0e0e0
  //   60747cf8f0f0e0e0 20703cf8f0f0f0e0 303870f0b0f0e0 1038707070f0ff 18303070fe20 183030f2e000
  //   101030f00000 101070400000 101070000000 101030000000 12*103000000000 7*1000000000 101000000000
  //   4*103000000000 206000000000 20e000000000 20e080000000 20e0c0000000 2060e0000101 202060000303
  //   2060000707 2020000707 2020000707 4*202020000707 202000000707 2020000707 2020000707 202000070f
  //   202000070f 2020000f0f 2020000f0f 2020000f0f 5*2020020f0f 2000020f0f 2020020f0f 20206000030f
  //   20206060000101 6060e0e0e00000 6060c0c0e0c000 c0c0c0e08080c0c0 c08080f080000000 c00080f820000000
  //   800080f828000000 80f8e8000000 f8e8000000 f8c8000000 10f8c0000000 38e0c0000000 38f8800000000800 80000
  //   8000000 0 800000000 80000000000 10b0f1f3f7fff ffefffffffffffff efffffffffffffff efffffffffffffff
  //   dfffffffffffffff cfffffffffffffff cf9fbfffffffffff ffffffffdfdfdfcf ffffefefdfdfffff
  //   ffffffc7ffffffff ffffffe7fbffffff fffffff3fbfbffff fffffffbfbfbffff fffffffbf9fbf9ff
  //   fffffffdfdfdfdff fffffdfdfdfdfdfd fffffdfdfdfdfdfd fffdfdfdfdfdfdfd fffdf9f9fdf9f9f9
  //   fff9fbf9f9f9f9f9 fffbfbfbf9fbfbf9 fffbfbfbfbfbfbfb fffbf3f3f3f3f3f3 fff3f7f3f3f3f3f3
  //   fff7f7f7f3f7f7f7 fff7e7e7f7f7f7e7 ffe7e7e7e7e7e7e7 ffefefefe7e7e7e7 ffefefefefefefe7
  //   ffefefcfefefefef ffefefcfefefefef ffefefc7efefefef ffefe7c7efefefcf ffefefc3cfcfcfcf
  //   ffefcfc3cfcfcfcf ffcfcfc3cfcfcfcf ffcfcfc3cfcfcfcf efcfcfc3cfcfcfcf ffcfcfc7c7cfcfcf
  //   ffcfcfcfc7cfcfcf ffcfcfcfcfc7cfcf ffcfcfcfcfcfcfcf ffcfcfcfcfcfcfcf ffcfcfcfcfcfcfcf
  //   ffcfcfcfcfcfc7c7 ffcfcfcfcfc787cf ffcfcfcfcfc3cfcf ffcfcfcfc3cfcfcf ffcfcfcfc3cfcfcf
  //   ffdfcfc3cfcfcfcf ffdf87c7cf8f8f8f ff9f878f8f8f8f8f ff9f978f8f8f8f8f ff9f9f97878f8f0f
  //   9f1f0f1f1f0f0f0f 1f1f0f1f1f170707 1f1f0f1f1b130707 1f1f0f1f17170707 1f0f0f1f1b130707
  //   9f1f0f1f1b1b0707 1f1f0f1f1b130707 1f1f0f1f1717070f 3f1f0f1f3b3b1707 3f3f1f3f7373370f
  //   7f3f7fefe7e7e74f ffffffefe7e7e7cf fffffffff3e3e3e7 ffdfdfcfc7c7e7cf ffffdfcfc7c7c7cf
  //   fffffff7f3e3e3c7 fffffff7e7e3e7c7 ffffffe7e7c7cf0f ffffffffe7c7c70f 3f3f7fff5707070f
  //   1f1f1f3f1703071f 9f8f8fdf83038f8f df8fcfcfcb01c7cf ffc7c7efe501e7e7 ffc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
endmodule
